// Digital circuit DemoP1.dig as structural Verilog
module DemoP1 (
  input  clk,
  input  in_2,
  input  in_3,
  input  in_8,
  output [6:0] out_4,
  output [6:0] out_5,
  output [6:0] out_6,
  output [6:0] out_7
);

  wire button_1_out, button_2_out, button_3_out, button_4_out, button_5_out, button_6_out, button_7_out,
       button_8_out, button_9_out, u_circuito_S1_acertou, u_circuito_S1_errou, u_circuito_S1_pronto;
  wire [6:0] u_ampSig_botoes;

  Button button_1 (.out(button_1_out));
  Button button_2 (.out(button_2_out));
  Button button_3 (.out(button_3_out));
  Button button_4 (.out(button_4_out));
  Button button_5 (.out(button_5_out));
  Button button_6 (.out(button_6_out));
  Button button_7 (.out(button_7_out));
  Button button_8 (.out(button_8_out));
  Button button_9 (.out(button_9_out));
  ampSig #(.applicationType("IVERILOG")) u_ampSig (
    .Botao1(button_2_out), .Botao2(button_3_out), .Botao3(button_4_out), .Botao4(button_5_out),
    .Botao5(button_6_out), .Botao6(button_8_out), .Botao7(button_9_out), .Botoes(u_ampSig_botoes));
  circuito_S1 #(.applicationType("IVERILOG")) u_circuito_S1 (
    .clock(clk), .reset(button_1_out), .jogar(button_7_out), .memoria(in_3), .nivel(in_2),
    .botoes(u_ampSig_botoes), .treinamento(in_8), .pronto(u_circuito_S1_pronto),
    .acertou(u_circuito_S1_acertou), .errou(u_circuito_S1_errou), .leds(out_7), .disp_hund(out_4),
    .disp_tens(out_5), .disp_ones(out_6));  // open: db_jogar, db_botoesIgualMemoria, db_tem_jogada, db_contagem, db_memoria, db_limite, db_jogadafeita, db_estado, db_timeout, db_clock
  LED led_1 (.in(u_circuito_S1_pronto));
  LED led_2 (.in(u_circuito_S1_acertou));
  LED led_3 (.in(u_circuito_S1_errou));

  // Notes on the sheet:
  //   clk: Hz: 1000
endmodule

/* Code of ampSig:
module ampSig (
	input Botao1,
	input Botao2,
	input Botao3,
	input Botao4,
	input Botao5,
	input Botao6,
	input Botao7,
	output [6:0] Botoes
);

assign Botoes = {Botao7, Botao6, Botao5, Botao4, Botao3, Botao2, Botao1};

endmodule
*/

/* Code of circuito_S1:
module circuito_S1 (
    input         clock,
    input         reset,
    input         jogar,
    input         memoria,
    input         nivel,
    input  [6:0]  botoes,
    input treinamento,
    output        pronto,
    output        acertou,
    output        errou,
    // Depuração
    output        db_jogar,
    output        db_botoesIgualMemoria,
    output        db_tem_jogada,
    output [6:0]  db_contagem,
    output [6:0]  db_memoria,
    output [6:0]  db_limite,
    output [6:0]  db_jogadafeita,
    output [6:0]  db_estado,
    output        db_timeout,
    output        db_clock,
    output [6:0]  leds,
    // Saída dos pontos – agora os pontos são exibidos em 3 displays de 7 segmentos
    output [6:0]  disp_hund, // display das centenas
    output [6:0]  disp_tens, // display das dezenas
    output [6:0]  disp_ones  // display das unidades
);

    // Sinais internos
    wire s_zeraR, s_registraR, s_contaE, s_zeraE, s_contaL, s_zeraL, s_fimL;
    wire [3:0] s_contagem;  // Contador de endereços (4 bits)
    wire [6:0] s_jogada;
    wire [3:0] s_limite;    // Contador de limite (4 bits)
    wire [6:0] s_memoria;
    wire [4:0] s_estado;
    // Agora s_pontos é de 8 bits para representar a pontuação de 0 a 255 (inicialmente 100)
    wire [7:0] s_pontos;
    wire s_enderecoIgualLimite;
    wire s_botoesIgualMemoria;
    wire s_jogadafeita;
    wire s_jogar;
    wire s_zeraT;
    wire s_contaT;
    wire s_timeout;
    wire s_zeraT2;
    wire s_contaT2;
    wire s_muda_leds;
    wire s_mostraJ, s_mostraB, s_mostraPontos, s_zeraPontos;
    wire s_zeraMemErro, s_contaErro, s_zeraErro, s_regErro, s_regPontos;

    // Instância do módulo de fluxo de dados
    S1_fluxo_dados FD(
        .clock (clock),
        .botoes (botoes),
        .zeraR (s_zeraR),
        .registraR (s_registraR),
        .contaE (s_contaE),
        .zeraE (s_zeraE),
        .contaL (s_contaL),
        .zeraL (s_zeraL),
        .enderecoIgualLimite (s_enderecoIgualMemoria),
        .botoesIgualMemoria (s_botoesIgualMemoria),
        .fimL (s_fimL),
        .fimE ( ),
        .memoria (memoria),
        .nivel (nivel),
        .zeraT(s_zeraT),
        .contaT(s_contaT),
        .timeout(s_timeout),
        .jogadafeita (s_jogadafeita),
        .db_limite (s_limite),
        .db_temjogada (db_tem_jogada),
        .db_contagem (s_contagem),
        .db_jogada (s_jogada),
        .db_memoria (s_memoria),
        .leds(leds),
        .zeraT2(s_zeraT2),
        .contaT2(s_contaT2),
        .mostraJ(s_mostraJ),
        .mostraB(s_mostraB),
        .muda_leds(s_muda_leds),
        .zeraPontos(s_zeraPontos),
        .pontos(s_pontos),
        .zeraMemErro (s_zeraMemErro),
        .contaErro(s_contaErro),
        .zeraErro(s_zeraErro),
        .regErro(s_regErro),
        .regPontos(s_regPontos)
    );

    // Instância do módulo de unidade de controle
    S1_unidade_controle UC(
        .clock (clock),
        .reset (reset),
        .jogar (s_jogar),
        .fimL (s_fimL),
        .enderecoIgualLimite (s_enderecoIgualMemoria),
        .botoesIgualMemoria (s_botoesIgualMemoria),
        .jogada (s_jogadafeita),
        .zeraE (s_zeraE),
        .contaE (s_contaE),
        .zeraL (s_zeraL),
        .contaL (s_contaL),
        .zeraR (s_zeraR),
        .registraR (s_registraR),
        .zeraT(s_zeraT),
        .contaT(s_contaT),
        .timeout(s_timeout),
        .pronto (pronto),
        .db_estado (s_estado),
        .db_timeout(db_timeout),
        .acertou (acertou),
        .serrou (errou),
        .zeraT2(s_zeraT2),
        .contaT2(s_contaT2),
        .mostraJ(s_mostraJ),
        .mostraB(s_mostraB),
        .muda_leds(s_muda_leds),
        .mostraPontos(s_mostraPontos),
        .zeraPontos(s_zeraPontos),
        .zeraMemErro (s_zeraMemErro),
        .contaErro(s_contaErro),
        .zeraErro(s_zeraErro),
        .regErro(s_regErro),
        .regPontos(s_regPontos),
        .treinamento(treinamento)
    );

    // Instâncias de módulos de depuração e exibição
    hexa7seg HEX0(
        .hexa (s_contagem),
        .display (db_contagem)
    );

    estado7seg HEX5(
        .estado (s_estado),
        .display (db_estado)
    );

    hexa7seg HEX3(
        .hexa(s_limite),
        .display (db_limite)
    );

    // O módulo edge_detector gera o sinal s_jogar a partir do sinal jogar
    edge_detector detector_borda(
        .clock(clock),
        .reset(reset),
        .sinal(jogar),
        .pulso(s_jogar)
    );
    
    // Sinais de depuração adicionais
    assign db_jogar = jogar;
    assign db_botoesIgualMemoria = s_botoesIgualMemoria;
    assign db_clock = clock;

    // Instancia o novo módulo display_pontos para exibir os pontos em 3 displays de 7 segmentos.
    display_pontos DP (
        .pontos(s_pontos),
        .enable(s_mostraPontos),
        .disp_hundreds(disp_hund),
        .disp_tens(disp_tens),
        .disp_ones(disp_ones)
    );
    
endmodule

/*---------------Laboratorio Digital-------------------------------------
 * Arquivo   : contador_m.v
 * Projeto   : Experiencia 4 - Desenvolvimento de Projeto de 
 *                             Circuitos Digitais em FPGA
 *-----------------------------------------------------------------------
 * Descricao : contador binario, modulo m, com parametros 
 *             M (modulo do contador) e N (numero de bits),
 *             sinais para clear assincrono (zera_as) e sincrono (zera_s)
 *             e saidas de fim e meio de contagem
 *             
 *-----------------------------------------------------------------------
 * Revisoes  :
 *     Data        Versao  Autor             Descricao
 *     30/01/2024  1.0     Edson Midorikawa  criacao
 *     16/01/2025  1.1     Edson Midorikawa  revisao
 *-----------------------------------------------------------------------
 * /

module contador_m #(parameter M=100, N=7)
  (
   input  wire          clock,
   input  wire          zera_as,
   input  wire          zera_s,
   input  wire          conta,
   output reg  [N-1:0]  Q,
   output reg           fim,
   output reg           meio
  );

  always @(posedge clock or posedge zera_as) begin
    if (zera_as) begin
      Q <= 0;
    end else if (clock) begin
      if (zera_s) begin
        Q <= 0;
      end else if (conta) begin
        if (Q == M-1) begin
          Q <= 0;
        end else begin
          Q <= Q + 1'b1;
        end
      end
    end
  end

  // Saidas
  always @ (Q)
      if (Q == M-1)   fim = 1;
      else            fim = 0;

  always @ (Q)
      if (Q == M/2-1) meio = 1;
      else            meio = 0;

endmodule
module display_pontos(
    input  [7:0] pontos,
    input        enable,
    output [6:0] disp_hundreds,
    output [6:0] disp_tens,
    output [6:0] disp_ones
);
    wire [3:0] hundreds;
    wire [3:0] tens;
    wire [3:0] ones;
    
    // Conversão de 8 bits para 3 dígitos BCD
    bin2bcd conv (
        .binary(pontos),
        .hundreds(hundreds),
        .tens(tens),
        .ones(ones)
    );
    
    // Se enable estiver ativo, passa os dígitos; caso contrário, envia um código (por exemplo, 10) para indicar blank.
    wire [3:0] hundreds_in = (enable) ? hundreds : 4'd10;
    wire [3:0] tens_in     = (enable) ? tens     : 4'd10;
    wire [3:0] ones_in     = (enable) ? ones     : 4'd10;
    
    // Instanciação de 3 módulos hexa7seg para cada dígito
    hexa7seg disp_hund_inst(
        .hexa(hundreds_in),
        .display(disp_hundreds)
    );
    
    hexa7seg disp_tens_inst(
        .hexa(tens_in),
        .display(disp_tens)
    );
    
    hexa7seg disp_ones_inst(
        .hexa(ones_in),
        .display(disp_ones)
    );
endmodule


module bin2bcd(
    input  [7:0] binary,
    output [3:0] hundreds,
    output [3:0] tens,
    output [3:0] ones
);
    // Divisão para extrair centenas, dezenas e unidades
    assign hundreds = binary / 100;
    assign tens     = (binary % 100) / 10;
    assign ones     = binary % 10;
endmodule
/*--------------------------------------------------------------
 * Arquivo   : estado7seg.v
 * Projeto   : Jogo do Desafio da Memoria
 * -------------------------------------------------------------
 * Descricao : decodificador estado para 
 *             display de 7 segmentos 
 * 
 * entrada: estado - codigo binario de 5 bits
 * saida: display - codigo de 7 bits para display de 7 segmentos
 * ----------------------------------------------------------------
 * dica de uso: mapeamento para displays da placa DE0-CV
 *              bit 6 mais significativo é o bit a esquerda
 *              p.ex. display(6) -> HEX0[6] ou HEX06
 * ----------------------------------------------------------------
 * Revisoes  :
 *     Data        Versao  Autor             	Descricao
 *     09/02/2021  1.0     Edson Midorikawa  	criacao
 *     30/01/2025  2.0     Edson Midorikawa  	revisao p/ Verilog
 * 	 11/02/2025  2.1 		Augusto Vaccarelli 	revisao
 * ----------------------------------------------------------------
 * /

module estado7seg (estado, display);
    input      [4:0] estado;
    output reg [6:0] display;


always @(*) begin
    case (estado)
        5'b00000: display = 7'b1000000;  // 0
        5'b00001: display = 7'b1111001;  // 1
        5'b00010: display = 7'b0100100;  // 2
        5'b00011: display = 7'b0110000;  // 3
        5'b00100: display = 7'b0011001;  // 4
        5'b00101: display = 7'b0010010;  // 5
        5'b00110: display = 7'b0000010;  // 6
        5'b00111: display = 7'b1111000;  // 7
        5'b01000: display = 7'b0000000;  // 8
        5'b01001: display = 7'b0010000;  // 9
        5'b01010: display = 7'b0001000;  // A
        5'b01011: display = 7'b0000011;  // B
        5'b01100: display = 7'b1000110;  // C
        5'b01101: display = 7'b0100001;  // D
        5'b01110: display = 7'b0000110;  // E
        5'b01111: display = 7'b0001110;  // F
        5'b10000: display = 7'b1111110;  // 10
        5'b10001: display = 7'b1111101;  // 11
        5'b10010: display = 7'b1111011;  // 12
        5'b10011: display = 7'b1110111;  // 13
        5'b10100: display = 7'b1101111;  // 14
        5'b10101: display = 7'b1011111;  // 15
        5'b10110: display = 7'b0111111;  // 16
        5'b10111: display = 7'b1111100;  // 17
        5'b11000: display = 7'b1110011;  // 18
        5'b11001: display = 7'b1100111;  // 19
        5'b11010: display = 7'b1001111;  // 1A
        5'b11011: display = 7'b0011111;  // 1B
        5'b11100: display = 7'b1110001;  // 1C
        5'b11101: display = 7'b1100011;  // 1D
        5'b11110: display = 7'b1000111;  // 1E
        5'b11111: display = 7'b0001111;  // 1F
        default:  display = 7'b1111111;
    endcase
end

endmodule


/* ----------------------------------------------------------------
 * Arquivo   : hexa7seg.v
 * Projeto   : Experiencia 2 - Um Fluxo de Dados Simples
 *--------------------------------------------------------------
 * Descricao : decodificador hexadecimal para 
 *             display de 7 segmentos 
 * 
 * entrada : hexa - codigo binario de 4 bits hexadecimal
 * saida   : sseg - codigo de 7 bits para display de 7 segmentos
 *
 * baseado no componente bcd7seg.v da Intel FPGA
 *--------------------------------------------------------------
 * dica de uso: mapeamento para displays da placa DE0-CV
 *              bit 6 mais significativo é o bit a esquerda
 *              p.ex. sseg(6) -> HEX0[6] ou HEX06
 *--------------------------------------------------------------
 * Revisoes  :
 *     Data        Versao  Autor             Descricao
 *     24/12/2023  1.0     Edson Midorikawa  criacao
 *--------------------------------------------------------------
 * /

module hexa7seg (hexa, display);
    input      [3:0] hexa;
    output reg [6:0] display;

    /*
     *    ---
     *   | 0 |
     * 5 |   | 1
     *   |   |
     *    ---
     *   | 6 |
     * 4 |   | 2
     *   |   |
     *    ---
     *     3
     * /
        
    always @(hexa)
    case (hexa)
        4'h0:    display = 7'b1000000;
        4'h1:    display = 7'b1111001;
        4'h2:    display = 7'b0100100;
        4'h3:    display = 7'b0110000;
        4'h4:    display = 7'b0011001;
        4'h5:    display = 7'b0010010;
        4'h6:    display = 7'b0000010;
        4'h7:    display = 7'b1111000;
        4'h8:    display = 7'b0000000;
        4'h9:    display = 7'b0010000;
        4'ha:    display = 7'b0001000;
        4'hb:    display = 7'b0000011;
        4'hc:    display = 7'b1000110;
        4'hd:    display = 7'b0100001;
        4'he:    display = 7'b0000110;
        4'hf:    display = 7'b0001110;
        default: display = 7'b1111111;
    endcase
endmodule


module mux2x1_7 (
    input   	[6:0]   D0,
    input   	[6:0]   D1,
    input     			  SEL,
    output reg [6:0]   OUT
);

always @(*) begin
    case (SEL)
        1'b0:    OUT = D0;
        1'b1:    OUT = D1;
        default: OUT = 7'b1111111; // saida em 1
    endcase
end

endmodule
/*------------------------------------------------------------------------
 * Arquivo   : mux2x1.v
 * Projeto   : Jogo do Desafio da Memoria
 *------------------------------------------------------------------------
 * Descricao : multiplexador 2x1
 * 
 * adaptado a partir do codigo my_4t1_mux.vhd do livro "Free Range VHDL"
 * 
 * exemplo de uso: ver testbench mux2x1_tb.v
 *------------------------------------------------------------------------
 * Revisoes  :
 *     Data        Versao  Autor             Descricao
 *     15/02/2024  1.0     Edson Midorikawa  criacao
 *     31/01/2025  1.1     Edson Midorikawa  revisao
 *------------------------------------------------------------------------
 * /

module mux2x1 (
    input   	[3:0]   D0,
    input   	[3:0]   D1,
    input     			  SEL,
    output reg [3:0]   OUT
);

always @(*) begin
    case (SEL)
        1'b0:    OUT = D0;
        1'b1:    OUT = D1;
        default: OUT = 4'b1111; // saida em 1
    endcase
end

endmodule
module S1_fluxo_dados (
    // Inputs
    input clock, //
    input [6:0] botoes,//
    // Sinais de Controle
    input zeraR,//
    input registraR,//
    input contaL,//
    input zeraL,//
    input contaE,//
    input zeraE,//
    input memoria,
	 input nivel,
    input zeraT,
    input contaT,
    input zeraT2,
    input contaT2,
    input mostraJ,
    input mostraB,
    input zeraMemErro,
    input contaErro,
    input zeraErro,
    input regErro,
    input zeraPontos,
    input regPontos,
    // Sinais de Condição
    output enderecoIgualLimite, //
    output botoesIgualMemoria,//
    output fimL,//
    output fimE, //
    output jogadafeita,//
    output timeout,
	 output muda_leds,
    // Depuração
    output db_temjogada,//
    output [3:0] db_limite, //
    output [3:0] db_contagem,//
    output [6:0] db_memoria,//
    output [6:0] db_jogada,//
	 output [6:0] leds,
	 output [7:0] pontos
);
    wire [6:0] s_jogada;  // sinal interno para interligacao dos componentes
    wire [3:0] s_contagem;
    wire [6:0] s_memoria;
    wire s_sinal;
    wire [3:0] s_limite;
    wire [6:0] s_memoria1;
    wire [6:0] s_memoria2;
    wire [6:0] s_mux;
    wire s_fim;
    wire [3:0] s_nivel = {nivel, 3'b111};
    wire [3:0] s_erros;
    wire [3:0] m_erros;
    assign s_sinal = botoes[0] | botoes[1] | botoes[2] | botoes[3] | botoes[4] | botoes[5] | botoes[6];
    wire [7:0] s_pontos, s_resultado;
    

     // ======================================================
    // Bloco de Contagem e Comparação da Sequência
    // ======================================================
    
    // Contador que marca o limite (número de jogadas na rodada)
    contador_163 ContLmt (
      .clock( clock ),
      .clr  ( ~zeraL ),
      .ld   ( 1'b1 ),
      .ent  ( 1'b1),
      .enp  ( contaL ),
      .D    ( 4'b0 ),
      .Q    ( s_limite ),
      .rco  (s_fim)
    );

    // Comparador para verificar se o limite (s_limite) atingiu o nível esperado
	  comparador_85 CompFim (
      .A   ( s_limite ),
      .B   ( s_nivel ),
      .ALBi( 1'b0 ),
      .AGBi( 1'b0 ),
      .AEBi( 1'b1 ),
      .ALBo(  ),
      .AGBo(  ),
      .AEBo( fimL )
    );

    // Contador para endereçamento (endereço na ROM)
    contador_163 ContEnd (
      .clock( clock ),
      .clr  ( ~zeraE ),
      .ld   ( 1'b1 ),
      .ent  ( 1'b1),
      .enp  ( contaE ),
      .D    ( 4'b0 ),
      .Q    ( s_contagem ),
      .rco  ( fimE )
    );
    
    // Comparador para verificar se o endereço é igual ao limite
    comparador_85 CompLmt (
      .A   ( s_limite ),
      .B   ( s_contagem ),
      .ALBi( 1'b0 ),
      .AGBi( 1'b0 ),
      .AEBi( 1'b1 ),
      .ALBo(  ),
      .AGBo(  ),
      .AEBo( enderecoIgualLimite )
    );

    // Registrador para armazenar a jogada dos botões (7 bits)
    registrador_7 RegBotoes (
      .clock  (clock),      
      .clear  (zeraR),      
      .enable (registraR),     
      .D      (botoes), 
      .Q      (s_jogada) 
    );

   // ROMs síncronas – memórias com a sequência esperada
    sync_rom_16x4_1 memoria1 (
      .clock (clock),
      .address (s_contagem),
      .data_out (s_memoria1)
    );
	 
	 sync_rom_16x4_2 memoria2 (
      .clock (clock),
      .address (s_contagem),
      .data_out (s_memoria2)
    );
    
    // MUX para selecionar entre as duas ROMs
    mux2x1_7 MUX_MEM (
		 .D0(s_memoria1),
		 .D1(s_memoria2),
		 .SEL(memoria),
		 .OUT(s_memoria)
	 );
	 
    // Comparador para verificar se a jogada registrada é igual à esperada
    comparador_85_7 CompJog (
      .A   ( s_memoria ),
      .B   ( s_jogada ),
      .ALBi( 1'b0 ),
      .AGBi( 1'b0 ),
      .AEBi( 1'b1 ),
      .ALBo(  ),
      .AGBo(  ),
      .AEBo( botoesIgualMemoria )
    );

    edge_detector detector_borda (
        .clock(clock),
        .reset(zeraR),
        .sinal(s_sinal),
        .pulso(jogadafeita)
    );

    // Contadores para timeout e atualização dos LEDs
    contador_m #(.M(5000), .N(13)) contador_5000(
        .clock (clock),
        .zera_as(1'b0),
        .zera_s (zeraT),
        .conta (contaT),
        .Q (),
        .fim (timeout),
        .meio () 

    );
	 contador_m #(.M(500), .N(13)) contador_500(
        .clock (clock),
        .zera_as(1'b0),
        .zera_s (zeraT2),
        .conta (contaT2),
        .Q (),
        .fim (muda_leds),
        .meio () 

    );
	// MUX para seleção de exibição: mostra a memória ou zero conforme mostraJ
	mux2x1_7 MUX (
        .D0(7'b0000000),
        .D1(s_memoria),
        .SEL(mostraJ),
        .OUT(s_mux)
	 );
	 
    // Segundo MUX: seleciona entre o resultado do MUX anterior e os botões para dirigir os LEDs
    mux2x1_7 MUX2 (
        .D0(s_mux),
        .D1(botoes),
        .SEL(mostraB),
        .OUT(leds)
	);

    // RAM síncrona para armazenamento dos erros (MemErro)
    sync_ram_16x4 MemErro (
        .clock(clock),
        .reset(zeraMemErro),
        .write_enable(regErro),
        .address (s_limite),
        .data_in(s_erros),
        .data_out(m_erros)
	);
	 
    // Contador de erros (acumula os erros durante a rodada)
    contador_163 ContErro (
        .clock( clock ),
        .clr  ( ~zeraErro ),
        .ld   ( 1'b1 ),
        .ent  ( 1'b1),
        .enp  ( contaErro ),
        .D    ( 4'b0 ),
        .Q    ( s_erros ),
        .rco  (  )
    );
	 
	// ======================================================
    // Lógica de Cálculo de Pontos
    // ======================================================
    // Registrador de pontos – ao ser "limpo" (clear) carrega o valor inicial de 100.
    registrador_8_init RegPontos (
      .clock  ( clock ),      
      .clear  ( zeraPontos ),      
      .enable ( regPontos ),     
      .D      ( s_resultado ), 
      .Q      ( s_pontos )
    );
    
    // Unidade aritmética para atualizar a parcial de pontos.
    // Observação: Durante a fase de pontuação, o mesmo contador (ContLmt) é reiniciado para iterar
    // sobre as posições de MemErro. Para cada iteração, considera-se que:
    //   round = s_limite + 1;         // round (1-based)
    //   round_factor = 16 - round;     // quanto menor o número da rodada, maior a dedução
    //   penalty = m_erros >> 1;        // m_erros * 0.5 (deslocamento à direita de 1 bit)
    // A nova parcial é: current_score - (round_factor * penalty)
    wire [4:0] round_num = {1'b0, s_limite} + 5'd1;  // converte s_limite (4 bits) para um número de rodada (1 a 16)
    wire [4:0] round_factor = 5'd16 - round_num;
    wire [3:0] penalty = m_erros >> 1;  // divisão por 2
    wire [8:0] deduction_temp = round_factor * penalty;  // produto (até 9 bits)
    wire [7:0] deduction = deduction_temp[7:0];  // dedução (8 bits)
    
    // Cálculo da nova parcial: s_pontos é o acumulador atual de pontos
    wire [7:0] calc_new_score = s_pontos - deduction;
    
    // A saída s_resultado da unidade aritmética é usada para atualizar o registrador de pontos
    assign s_resultado = calc_new_score;
	 

    // saidas de depuracao
    assign db_limite = s_limite;
    assign db_temjogada = s_sinal;
    assign db_contagem = s_contagem;
    assign db_memoria = s_memoria;
    assign db_jogada = s_jogada;
	assign pontos = s_pontos;
 endmodule
 
module registrador_7 (
    input        clock,
    input        clear,
    input        enable,
    input  [6:0] D,
    output [6:0] Q
);

    reg [6:0] IQ;

    always @(posedge clock or posedge clear) begin
        if (clear)
            IQ <= 0;
        else if (enable)
            IQ <= D;
    end

    assign Q = IQ;

endmodule

// ======================================================
// MÓDULO: registrador_8_init
// ======================================================
// Ao receber clear, carrega 100; em enable, atualiza com D.
module registrador_8_init (
    input        clock,
    input        clear,
    input        enable,
    input  [7:0] D,
    output reg [7:0] Q
);
    always @(posedge clock or posedge clear) begin
        if (clear)
            Q <= 8'd100;  // inicializa com 100 pontos
        else if (enable)
            Q <= D;
    end
endmodule


module sync_rom_16x4_1 (clock, address, data_out);
    input            clock;
    input      [3:0] address;
    output reg [6:0] data_out;

    always @ (posedge clock)
    begin
        case (address)
            4'b0000: data_out = 7'b0000001;
            4'b0001: data_out = 7'b0000010;
            4'b0010: data_out = 7'b0000100;
            4'b0011: data_out = 7'b0001000;
            4'b0100: data_out = 7'b0010000;
            4'b0101: data_out = 7'b0100000;
            4'b0110: data_out = 7'b1000000;
            4'b0111: data_out = 7'b0100000;
            4'b1000: data_out = 7'b0010000;
            4'b1001: data_out = 7'b0001000;
            4'b1010: data_out = 7'b0000100;
            4'b1011: data_out = 7'b0000010;
            4'b1100: data_out = 7'b0000001;
            4'b1101: data_out = 7'b0000010;
            4'b1110: data_out = 7'b0000100;
            4'b1111: data_out = 7'b0001000;
        endcase
    end
endmodule

module sync_rom_16x4_2 (clock, address, data_out);
    input            clock;
    input      [3:0] address;
    output reg [6:0] data_out;

    always @ (posedge clock)
    begin
        case (address)
            4'b0000: data_out = 7'b0000001;
            4'b0001: data_out = 7'b0000010;
            4'b0010: data_out = 7'b0000100;
            4'b0011: data_out = 7'b0001000;
            4'b0100: data_out = 7'b0010000;
            4'b0101: data_out = 7'b0100000;
            4'b0110: data_out = 7'b1000000;
            4'b0111: data_out = 7'b0100000;
            4'b1000: data_out = 7'b0010000;
            4'b1001: data_out = 7'b0001000;
            4'b1010: data_out = 7'b0000100;
            4'b1011: data_out = 7'b0000010;
            4'b1100: data_out = 7'b0000001;
            4'b1101: data_out = 7'b0000010;
            4'b1110: data_out = 7'b0000100;
            4'b1111: data_out = 7'b0001000;
        endcase
    end
endmodule

module sync_ram_16x4 (
    input            clock,
    input            reset,        // Novo sinal de reset síncrono
    input            write_enable,
    input      [3:0] address,
    input      [3:0] data_in,
    output reg [3:0] data_out
);
    reg [3:0] ram_block [0:15]; 

    integer i; // variável para o for

    always @(posedge clock) begin
        if (reset) begin
            // Zera toda a memória
            for (i = 0; i < 16; i = i + 1)
                ram_block[i] <= 4'b0000;
            // Zera a saída também
            data_out <= 4'b0000;
        end else begin
            // Operação normal de escrita
            // (só ocorre se address não estiver em 'x')
            if (write_enable && (address !== 4'bx))
                ram_block[address] <= data_in;

            // Proteção contra endereço indefinido
            if (address === 4'bx)
                data_out <= 4'b0000;
            else
                data_out <= ram_block[address];
        end
    end
endmodule




module comparador_85 (ALBi, AGBi, AEBi, A, B, ALBo, AGBo, AEBo);

    input[3:0] A, B;
    input      ALBi, AGBi, AEBi;
    output     ALBo, AGBo, AEBo;
    wire[4:0]  CSL, CSG;

    assign CSL  = ~A + B + ALBi;
    assign ALBo = ~CSL[4];
    assign CSG  = A + ~B + AGBi;
    assign AGBo = ~CSG[4];
    assign AEBo = ((A == B) && AEBi);

endmodule /* comparador_85 * /

module comparador_85_7 (ALBi, AGBi, AEBi, A, B, ALBo, AGBo, AEBo);

    input[6:0] A, B;
    input      ALBi, AGBi, AEBi;
    output     ALBo, AGBo, AEBo;
    wire[7:0]  CSL, CSG;

    assign CSL  = ~A + B + ALBi;
    assign ALBo = ~CSL[7];
    assign CSG  = A + ~B + AGBi;
    assign AGBo = ~CSG[7];
    assign AEBo = ((A == B) && AEBi);

endmodule /* comparador_85 * /

module contador_163 ( clock, clr, ld, ent, enp, D, Q, rco );
    input clock, clr, ld, ent, enp;
    input [3:0] D;
    output reg [3:0] Q;
    output reg rco;

    always @ (posedge clock)
        if (~clr)               Q <= 4'd0;
        else if (~ld)           Q <= D;
        else if (ent && enp)    Q <= Q + 1'b1;
        else                    Q <= Q;
 
    always @ (Q or ent)
        if (ent && (Q == 4'd15))   rco = 1;
        else                       rco = 0;
endmodule

module edge_detector (
    input  clock,
    input  reset,
    input  sinal,
    output pulso
);

    reg reg0;
    reg reg1;

    always @(posedge clock or posedge reset) begin
        if (reset) begin
            reg0 <= 1'b0;
            reg1 <= 1'b0;
        end else if (clock) begin
            reg0 <= sinal;
            reg1 <= reg0;
        end
    end

    assign pulso = ~reg1 & reg0;

endmodule
module S1_unidade_controle (
    input      clock,    // clock do sistema
    input      reset,    // reset assíncrono
    input      jogar,    // sinal para iniciar o jogo
    input      fimL,     // sinal que indica que o contador de limite atingiu seu valor máximo (fim da contagem da rodada ou fim do jogo)
    input      botoesIgualMemoria,  // resultado da comparação entre a jogada e a sequência armazenada
    input      enderecoIgualLimite, // indica se o endereço (contagem) atingiu o limite esperado
    input      jogada,   // sinal que indica que a jogada foi efetivada (detectada a borda)
    input      timeout,  // sinal de tempo esgotado
    input      muda_leds,// sinal que indica que os LEDs já foram atualizados
    input treinamento,
    output reg zeraT,     // zera temporizador T
    output reg contaT,    // conta temporizador T
    output reg zeraE,     // zera o contador de endereços (usado na leitura da memória)
    output reg contaE,    // incrementa o contador de endereços
    output reg zeraL,     // zera o contador de limite (que marca o tamanho da sequência ou o número da rodada)
    output reg contaL,    // incrementa o contador de limite
    output reg zeraR,     // zera o registrador de jogada
    output reg registraR, // habilita o registrador de jogada
    output reg pronto,    // sinal que indica que o jogo terminou (por acerto ou timeout)
    output reg [4:0] db_estado,  // para depuração: exibe o estado atual da FSM
    output reg acertou,   // sinaliza que a rodada foi concluída sem erros
    output reg serrou,    // sinaliza que houve erro na jogada
    output reg db_timeout,// depuração: indica timeout
    output reg mostraJ,   // controla a exibição dos LEDs (modo “jogada”)
    output reg mostraB,   // controla a exibição dos botões (modo “botão”)
    output reg zeraT2,    // zera temporizador T2 (para atualização dos LEDs)
    output reg contaT2,   // incrementa temporizador T2
    output reg mostraPontos, // ativa a exibição dos pontos
    output reg zeraMemErro,
    output reg contaErro, // incrementa o contador de erros
    output reg zeraErro,  // zera o contador de erros
    output reg regErro,   // registra (salva) o valor de erro na memória
    output reg zeraPontos,// clear no registrador de pontos (inicia com 100)
    output reg regPontos  // atualiza o registrador de pontos com o novo valor parcial
);

    //=============================================================
    // Definição dos estados
    //=============================================================
    parameter inicial        = 5'b00000; // 0
    parameter preparacao     = 5'b00001; // 1
    parameter espera_jogada  = 5'b00011; // 3
    parameter registra       = 5'b00100; // 4
    parameter comparacao     = 5'b00101; // 5
    parameter proximo        = 5'b00110; // 6
    parameter mostra_leds    = 5'b00111; // 7
    parameter comparaJ       = 5'b01000; // 8
    parameter incrementaE    = 5'b01001; // 9
    parameter preparaE       = 5'b01100; // C
    parameter fim_rodada     = 5'b01011; // B
    parameter prox_rodada    = 5'b00010; // 2
    parameter errou          = 5'b01110; // E
    parameter fim_acertou    = 5'b01010; // A
    parameter fim_timeout    = 5'b01101; // D
    parameter calc_pontos    = 5'b10000; // 16
    parameter salva_pontos   = 5'b10001; // 17
    parameter prox_pos       = 5'b10010; // 18
    parameter prep_fim       = 5'b10011; // 19
    parameter modo_treino    = 5'b10100;

    //=============================================================
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*/
